// Logisim project bit16.circ as structural Verilog: 1 circuit, main circuit main
module main (
  input  Hep_0,
  input  Hep_1,
  input  Hep_0_2,
  input  Jump,
  input  [15:0] Data_In,
  input  Count_Enable,
  input  Reset,
  input  in_8,
  input  [15:0] in_9,
  input  Hep_0_3,
  input  Hep_0_4,
  input  Hep_0_5,
  output [2:0] \Hangi_Register_Yazma_İşlemi ,
  output [15:0] out_14,
  output [15:0] out_15,
  output [15:0] out_16,
  output [15:0] out_17,
  output [4:0] Immadiate,
  output [2:0] Src_Reg,
  output [2:0] Dest_Reg,
  output [4:0] Opcode,
  output [15:0] out_22,
  output [15:0] \Sonuç 
);

  wire and_1_out, and_2_out, clock_2_out, clock_3_out, clock_4_out, Clock_out, comparator_1_eq,
       demultiplexer_1_out0, demultiplexer_1_out1, demultiplexer_1_out2, demultiplexer_1_out3,
       demultiplexer_1_out4, demultiplexer_1_out5, demultiplexer_1_out6, demultiplexer_1_out7, not_1_out,
       not_2_out, not_3_out, or_1_out, or_2_out, or_3_out, or_4_out, or_5_out, or_6_out, or_7_out, or_8_out;
  wire [15:0] counter_1_q, demultiplexer_2_out0, demultiplexer_2_out1, demultiplexer_2_out2,
       demultiplexer_2_out3, demultiplexer_2_out4, demultiplexer_2_out5, demultiplexer_2_out6,
       demultiplexer_2_out7, or_9_out, R0_q, R1_q, R2_q, R3_q, R4_q, R5_q, R6_q, R7_q, ram_2_data,
       subtractor_1_out;

  Counter #(.width(16), .max('hffff)) counter_1 (
    .load(Jump), .D(Data_In), .count(Count_Enable), .Q(counter_1_q), .clk(Clock_out), .clr(Reset));  // open: carry
  Clock Clock (.out(Clock_out));
  Multiplexer #(.width(16)) multiplexer_1 (
    .in0(counter_1_q), .out(out_15), .sel(Hep_0_4), .en(not_2_out));  // open: in1
  Clock clock_2 (.out(clock_2_out));
  not not_1 (not_1_out, in_8);
  not not_2 (not_2_out, and_2_out);
  Multiplexer #(.width(16)) multiplexer_2 (
    .in0(in_9), .out({Opcode, Dest_Reg, Src_Reg, Immadiate}), .sel(Hep_0_3), .en(not_1_out));  // open: in1
  Multiplexer #(.width(16)) multiplexer_3 (
    .in0({{11{Hep_0_2}}, Immadiate}), .out(out_15), .sel(Hep_0_5), .en(and_2_out));  // open: in1
  RAM #(.addrWidth(16), .dataWidth(16)) ram_1 (
    .addr(out_15), .data({Opcode, Dest_Reg, Src_Reg, Immadiate}), .clk(clock_2_out), .ld(in_8));  // open: sel, clr
  and and_1 (and_1_out, Opcode[0], Opcode[1]);
  and and_2 (and_2_out, and_1_out, not_3_out);
  Demultiplexer #(.select(3)) demultiplexer_1 (
    .out0(demultiplexer_1_out0), .out1(demultiplexer_1_out1), .out2(demultiplexer_1_out2),
    .out3(demultiplexer_1_out3), .out4(demultiplexer_1_out4), .out5(demultiplexer_1_out5),
    .out6(demultiplexer_1_out6), .out7(demultiplexer_1_out7), .in(Hep_1), .sel(Dest_Reg));  // open: en
  or or_1 (or_1_out, demultiplexer_1_out0, Hep_0);
  or or_2 (or_2_out, demultiplexer_1_out1, Hep_0);
  or or_3 (or_3_out, demultiplexer_1_out2, Hep_0);
  or or_4 (or_4_out, demultiplexer_1_out3, Hep_0);
  or or_5 (or_5_out, demultiplexer_1_out4, Hep_0);
  or or_6 (or_6_out, demultiplexer_1_out5, Hep_0);
  or or_7 (or_7_out, demultiplexer_1_out6, Hep_0);
  or or_8 (or_8_out, demultiplexer_1_out7, Hep_0);
  Demultiplexer #(.select(3), .width(16)) demultiplexer_2 (
    .out0(demultiplexer_2_out0), .out1(demultiplexer_2_out1), .out2(demultiplexer_2_out2),
    .out3(demultiplexer_2_out3), .out4(demultiplexer_2_out4), .out5(demultiplexer_2_out5),
    .out6(demultiplexer_2_out6), .out7(demultiplexer_2_out7), .in(out_14), .sel(Dest_Reg));  // open: en
  Register #(.width(16)) R0 (.D(demultiplexer_2_out0), .en(or_1_out), .Q(R0_q), .clk(clock_3_out));  // open: clr
  Register #(.width(16)) R1 (.D(demultiplexer_2_out1), .en(or_2_out), .Q(R1_q), .clk(clock_3_out));  // open: clr
  Register #(.width(16)) R2 (.D(demultiplexer_2_out2), .en(or_3_out), .Q(R2_q), .clk(clock_3_out));  // open: clr
  Register #(.width(16)) R3 (.D(demultiplexer_2_out3), .en(or_4_out), .Q(R3_q), .clk(clock_3_out));  // open: clr
  Register #(.width(16)) R4 (.D(demultiplexer_2_out4), .en(or_5_out), .Q(R4_q), .clk(clock_3_out));  // open: clr
  Register #(.width(16)) R5 (.D(demultiplexer_2_out5), .en(or_6_out), .Q(R5_q), .clk(clock_3_out));  // open: clr
  Register #(.width(16)) R6 (.D(demultiplexer_2_out6), .en(or_7_out), .Q(R6_q), .clk(clock_3_out));  // open: clr
  Register #(.width(16)) R7 (.D(demultiplexer_2_out7), .en(or_8_out), .Q(R7_q), .clk(clock_3_out));  // open: clr
  Clock clock_3 (.out(clock_3_out));
  Multiplexer #(.select(3), .width(16)) multiplexer_4 (
    .in0(R0_q), .in1(R1_q), .in2(R2_q), .in3(R3_q), .in4(R4_q), .in5(R5_q), .in6(R6_q), .in7(R7_q),
    .out(out_16), .sel(Dest_Reg));  // open: en
  Multiplexer #(.select(3), .width(16)) multiplexer_5 (
    .in0(R0_q), .in1(R1_q), .in2(R2_q), .in3(R3_q), .in4(R4_q), .in5(R5_q), .in6(R6_q), .in7(R7_q),
    .out(out_22), .sel(Src_Reg));  // open: en
  Subtractor #(.width(16)) subtractor_1 (
    .a(out_22), .b({{11{Hep_0_2}}, Immadiate}), .out(subtractor_1_out));  // open: bin, bout
  Clock clock_4 (.out(clock_4_out));
  Comparator #(.width(16)) comparator_1 (.a(out_16), .b(out_22), .eq(comparator_1_eq));  // open: gt, lt
  assign or_9_out = out_22 | {{11{Hep_0_2}}, Immadiate};  // OR_Gate or_9, 16 bits wide
  RAM #(.addrWidth(16), .dataWidth(16), .bus("separate")) ram_2 (
    .addr(out_22), .din({{11{Hep_0_2}}, Immadiate}), .data(ram_2_data), .clk(clock_4_out));  // open: str, sel, ld, clr
  not not_3 (not_3_out, comparator_1_eq);
  Multiplexer #(.select(5), .width(16)) multiplexer_6 (
    .in0(subtractor_1_out), .in1(or_9_out), .in2(ram_2_data), .out(out_14), .sel(Opcode));  // open: in3, in4, in5, in6, in7, in8, in9, in10, in11, in12, in13, in14, in15, in16, in17, in18, in19, in20, in21, in22, in23, in24, in25, in26, in27, in28, in29, in30, in31, en

  assign \Hangi_Register_Yazma_İşlemi  = Dest_Reg;
  assign out_17 = {{11{Hep_0_2}}, Immadiate};
  assign \Sonuç  = out_14;

  // Notes on the sheet:
  //   SUBI: SOURCE - IMMADIATE
  //   ORI : IMMADIATE - SOURCE
  //   BRANCH: DES VS SOURCE
  //   ımmadiate de verilen adrese yazar
  //   STR: SOURCE: ADRES IMMADIATE: VALUE DEST REG: SONUÇ
  //   0: Store <-
  //   1: Load ->
  //   İnstruction Kodu
  //   Bu pin 1 ise load 0 ise store
  //   immediate: adres
  //   15:11 -> Opcode
  //   10:8 -> Dest Reg (Sonucun Yazıldığı Yer)
  //   7:5 -> Src Reg (ALU ya gidicek)
  //   4:0 -> Immediate
  //   Branch geldi: 11 ve 12(BNE için)
  //   Branch burdan gelir
  //   Eşitse 0 eşit değilse 1
  //   # sayi
  //   hangi register
  //   hedef register
  //   yapılan işlem
  //   Demux Dest Reg bilgisine göre sadece bir register a yazma izni verir.
  //   Write Address
  //   ALU nun 2. girişi
  //   Write Address
  //   Read Register 1
  //   Read Register
  //   ALU ya gidicek
  //   dest reg
  //   ALU Giriş 1
  //   ALU Giriş 2 
  //   Eşit değilse 1 verir
  //   Eşitse 0 verir
  //   Read Register 2
  //   source reg
  //   adress: soruce reg data:immediate dest:sonuç
  //   STR
  //   SUBI
  //   ORI
endmodule
